# Fritzing sketch aqua-sensor-circuit (saved by Fritzing 0.9.3b)
circuit board: 4.31442cm x 6.08318cm

parts:
  MC = Arduino Pro Mini v13
  nrf = NRF24L01+ Breakout Board
  J1 = female pin header, 3 pins [form="♀ (female)"]
  J3 = female pin header, 3 pins [form="♀ (female)"]
  J4 = female pin header, 2 pins [form="♀ (female)"]
  J5 = female pin header, 3 pins [form="♀ (female)"]
  R1 = Resistor [tolerance=±5% resistance=1k package=THT]
  C1 = Ceramic Capacitor [capacitance=10nF package="200 mil [THT, multilayer]"]
  C2 = Ceramic Capacitor [capacitance=10nF package="200 mil [THT, multilayer]"]
  R2 = Resistor [tolerance=±5% resistance=1k package=THT]
  C3 = Ceramic Capacitor [capacitance=10nF package="200 mil [THT, multilayer]"]
  R3 = Resistor [tolerance=±5% resistance=1k package=THT]
  J6 = female pin header, 2 pins [form="♀ (female)"]

nets:
  N1: MC.VCC, J1.pin1, J3.pin1, J5.pin1, R1.Pin_1, R2.Pin_1, R3.Pin_0, J6.pin1
  GND: MC.GND, nrf.GND, J1.pin2, J3.pin3, J4.pin2, J5.pin2, C1.1, C2.1, C3.1, J6.pin2
  N2: MC.D13/SCK, nrf.SCK
  N3: MC.D12/MISO, nrf.MISO
  N4: MC.D11_PWM/MOSI, nrf.MOSI
  N5: MC.D10_PWM/SS, nrf.CS
  N6: MC.D9_PWM, nrf.CE
  N7: MC.D4, J4.pin1, C1.0, R2.Pin_0
  N8: MC.D3_PWM, J1.pin3, C2.0, R3.Pin_1
  N9: MC.D2, J5.pin3, R1.Pin_0, C3.0
  N10: nrf.VCC, J3.pin2
